// Digital circuit ex1.dig as structural Verilog
module ex1 (
  input  A,
  input  B,
  input  C,
  output X,
  output Y,
  output Z
);

  wire and_1_out, and_2_out, and_3_out, and_4_out, and_5_out, and_6_out, and_7_out, and_8_out, and_9_out,
       and_10_out, not_1_out, not_2_out, not_3_out;

  not not_1 (not_1_out, A);
  not not_2 (not_2_out, B);
  not not_3 (not_3_out, C);
  and and_1 (and_1_out, A, B);
  and and_2 (and_2_out, not_1_out, not_3_out);
  and and_3 (and_3_out, not_3_out, B);
  and and_4 (and_4_out, A, not_2_out, not_3_out);
  and and_5 (and_5_out, not_2_out, C);
  and and_6 (and_6_out, not_3_out, B);
  and and_7 (and_7_out, not_1_out, not_2_out, not_3_out);
  and and_8 (and_8_out, A, B, C);
  and and_9 (and_9_out, A, not_2_out, C);
  and and_10 (and_10_out, not_1_out, not_2_out, not_3_out);
  or or_1 (X, and_1_out, and_2_out, and_3_out);
  or or_2 (Y, and_4_out, and_5_out, and_6_out, and_7_out);
  or or_3 (Z, and_8_out, and_9_out, and_10_out);
endmodule

/* Test case EX1 Test:
A B C X Y Z

loop(A,2)
   loop(B,2)
      loop(C,2)
         bits(1,A) bits(1,B) bits(1,C) bits(1, (!A&!C) | (A&B)) bits(1, !B|!C) bits(1, (!A&!B&!C) | (A&C))
      end loop
   end loop
end loop
*/
