// Digital circuit Lab02.dig as structural Verilog
module Lab02 (
  input  B,
  input  C,
  input  A,
  input  D,
  output Fa,
  output Fb,
  output Fc,
  output Fd,
  output Fe,
  output Fg,
  output Ff
);

  wire AB, AC, ADnC, AnB, AnBnC, AnC, BC, BCD, BCnD, BDnA, BDnC, BnA, BnAnC, BnAnD, BnC, CDnA, CDnB, CnA,
       CnB, CnD, DnA, DnC, nA, nAnB, nAnBnD, nAnC, nAnCnD, nB, nBnC, nBnD, nC, nCnD, nD;

  not not_1 (nA, A);
  not not_2 (nB, B);
  not not_3 (nC, C);
  not not_4 (nD, D);
  and and_1 (BC, B, C);
  and and_2 (CnA, C, nA);
  and and_3 (nBnD, nB, nD);
  and and_4 (nAnB, nA, nB);
  and and_5 (AnB, A, nB);
  and and_6 (BnA, B, nA);
  and and_7 (DnA, D, nA);
  and and_8 (DnC, D, nC);
  and and_9 (nAnC, nA, nC);
  and and_10 (AnC, A, nC);
  and and_11 (AB, A, B);
  and and_12 (AC, A, C);
  and and_13 (CnD, C, nD);
  and and_14 (nAnC, nA, nC);
  and and_15 (BnC, B, nC);
  and and_16 (CnB, C, nB);
  and and_17 (nBnC, nC, nB);
  and and_18 (nCnD, nC, nD);
  and and_19 (BDnA, B, D, nA);
  and and_20 (AnBnC, A, nB, nC);
  and and_21 (ADnC, A, D, nC);
  and and_22 (CDnA, C, D, nA);
  and and_23 (nAnCnD, nA, nD, nC);
  and and_24 (BCnD, B, C, nD);
  and and_25 (BDnC, B, D, nC);
  and and_26 (CDnB, C, D, nB);
  and and_27 (nAnBnD, nA, nB, nD);
  and and_28 (BnAnC, nA, B, nC);
  and and_29 (BnAnD, nA, nD, B);
  and and_30 (nAnCnD, nA, nD, nC);
  and and_31 (BCD, B, C, D);
  or or_1 (Fa, A, nBnC, nCnD, BCD);
  or or_2 (Fb, nAnB, nBnD, ADnC, CDnA, nAnCnD);
  or or_3 (Fc, nAnCnD, nAnCnD, nAnCnD, nAnCnD, nAnCnD);
  or or_4 (Fd, nAnCnD, nAnCnD, nAnCnD, nAnCnD, nAnCnD);
  or or_5 (Fe, nAnCnD, nAnCnD, nAnCnD, nAnCnD);
  or or_6 (Ff, nAnCnD, nAnCnD, nAnCnD, nAnCnD, nAnCnD);
  or or_7 (Fg, nAnCnD, nAnCnD, nAnCnD, nAnCnD);
  Seven_Seg seven_seg_1 (.a(Fa), .b(Fb), .c(Fc), .d(Fd), .e(Fe), .f(Ff), .g(Fg), .dp(1'b0));
endmodule
