// Digital circuit add-sub.dig as structural Verilog
module add_sub (
  input  [31:0] B,
  input  [31:0] A,
  input  Sub,
  output [31:0] Out,
  output Overflow,
  output Sign
);

  wire and_1_out, and_2_out, multiplexer_2_out, not_33_out, not_34_out, not_35_out;
  wire [31:0] Add_s, not_1_out, NOT_B__plus_1, Subtract_s;

  Add #(.Bits(32)) Add (.a(A), .b(B), .c_i(1'b0), .s(Add_s));  // open: c_o
  not not_1 (not_1_out[0], B[0]);
  not not_2 (not_1_out[1], B[1]);
  not not_3 (not_1_out[2], B[2]);
  not not_4 (not_1_out[3], B[3]);
  not not_5 (not_1_out[4], B[4]);
  not not_6 (not_1_out[5], B[5]);
  not not_7 (not_1_out[6], B[6]);
  not not_8 (not_1_out[7], B[7]);
  not not_9 (not_1_out[8], B[8]);
  not not_10 (not_1_out[9], B[9]);
  not not_11 (not_1_out[10], B[10]);
  not not_12 (not_1_out[11], B[11]);
  not not_13 (not_1_out[12], B[12]);
  not not_14 (not_1_out[13], B[13]);
  not not_15 (not_1_out[14], B[14]);
  not not_16 (not_1_out[15], B[15]);
  not not_17 (not_1_out[16], B[16]);
  not not_18 (not_1_out[17], B[17]);
  not not_19 (not_1_out[18], B[18]);
  not not_20 (not_1_out[19], B[19]);
  not not_21 (not_1_out[20], B[20]);
  not not_22 (not_1_out[21], B[21]);
  not not_23 (not_1_out[22], B[22]);
  not not_24 (not_1_out[23], B[23]);
  not not_25 (not_1_out[24], B[24]);
  not not_26 (not_1_out[25], B[25]);
  not not_27 (not_1_out[26], B[26]);
  not not_28 (not_1_out[27], B[27]);
  not not_29 (not_1_out[28], B[28]);
  not not_30 (not_1_out[29], B[29]);
  not not_31 (not_1_out[30], B[30]);
  not not_32 (not_1_out[31], B[31]);
  Add #(.Bits(32)) Subtract (.a(A), .b(not_1_out), .c_i(1'b1), .s(Subtract_s));  // open: c_o
  Add #(.Bits(32)) add_2 (.a(not_1_out), .b(32'h1), .c_i(1'b0), .s(NOT_B__plus_1));  // open: c_o
  Multiplexer #(.Bits(32)) multiplexer_1 (.sel(Sub), .in_0(Add_s), .in_1(Subtract_s), .out(Out));
  Multiplexer multiplexer_2 (.sel(Sub), .in_0(B[31]), .in_1(NOT_B__plus_1[31]), .out(multiplexer_2_out));
  and and_1 (and_1_out, A[31], multiplexer_2_out, not_33_out);
  not not_33 (not_33_out, Out[31]);
  not not_34 (not_34_out, A[31]);
  not not_35 (not_35_out, multiplexer_2_out);
  and and_2 (and_2_out, not_34_out, not_35_out, Out[31]);
  or or_1 (Overflow, and_1_out, and_2_out);

  assign Sign = Out[31];

  // Other names for the same wires on the sheet: SIGN_A = A[31]; SIGN_B = B[31]; SIGN_OUT = Out[31]
endmodule

/* Test case Add-Sub Test:
A B Sub Out Overflow Sign
0x289322C4 0x01846399 0 0x2A17865D 0 0
0x4152A22D 0x22042121 0 0x6356C34E 0 0
0x84893212 0x0994AD1A 0 0x8E1DDF2C 0 1
0x90A8826C 0x112109FB 0 0xA1C98C67 0 1
0x5210C12D 0x3D04ABBC 0 0x8F156CE9 1 1
0x90D194B5 0xB005500E 0 0x40D6E4C3 1 0
0x39332544 0x0435FCAD 1 0x34FD2897 0 0
0x59286AB1 0x221FB76C 1 0x3708B345 0 0
0xECD55935 0x248C5A4B 1 0xC848FEEA 0 1
0x902A9525 0xE5454D48 1 0xAAE547DD 0 1
0x8211036A 0x7B13890A 1 0x06FD7A60 1 0
0x5FE15DBE 0x8934B9B1 1 0xD6ACA40D 1 1
*/
