// Digital circuit register-file.dig as structural Verilog
module register_file (
  input  [4:0] ReadReg1,
  input  [4:0] ReadReg2,
  input  [4:0] WriteReg,
  input  [31:0] WriteData,
  input  RegWrite,
  input  Clock,
  output [31:0] ReadData1,
  output [31:0] ReadData2
);

  wire in1, in2, in3, in4, in5, in6, in7, in8, in9, in10, in11, in12, in13, in14, in15, in16, in17, in18,
       in19, in20, in21, in22, in23, in24, in25, in26, in27, in28, in29, in30, in31, y0, y1, y2, y3, y4, y5,
       y6, y7, y8, y9, y10, y11, y12, y13, y14, y15, y16, y17, y18, y19, y20, y21, y22, y23, y24, y25, y26,
       y27, y28, y29, y30, y31;
  wire [31:0] Reg0out, Reg1out, Reg2out, Reg3out, Reg4out, Reg5out, Reg6out, Reg7out, Reg8out, Reg9out,
       Reg10out, Reg11out, Reg12out, Reg13out, Reg14out, Reg15out, Reg16out, Reg17out, Reg18out, Reg19out,
       Reg20out, Reg21out, Reg22out, Reg23out, Reg24out, Reg25out, Reg26out, Reg27out, Reg28out, Reg29out,
       Reg30out, Reg31out;

  Decoder #(.Selector_Bits(5)) decoder_1 (
    .sel(WriteReg), .out_0(y0), .out_1(y1), .out_2(y2), .out_3(y3), .out_4(y4), .out_5(y5), .out_6(y6),
    .out_7(y7), .out_8(y8), .out_9(y9), .out_10(y10), .out_11(y11), .out_12(y12), .out_13(y13), .out_14(y14),
    .out_15(y15), .out_16(y16), .out_17(y17), .out_18(y18), .out_19(y19), .out_20(y20), .out_21(y21),
    .out_22(y22), .out_23(y23), .out_24(y24), .out_25(y25), .out_26(y26), .out_27(y27), .out_28(y28),
    .out_29(y29), .out_30(y30), .out_31(y31));
  and and_1 (in1, y1, RegWrite);
  and and_2 (in4, y4, RegWrite);
  and and_3 (in7, y7, RegWrite);
  and and_4 (in10, y10, RegWrite);
  and and_5 (in13, y13, RegWrite);
  and and_6 (in16, y16, RegWrite);
  and and_7 (in19, y19, RegWrite);
  and and_8 (in22, y22, RegWrite);
  and and_9 (in25, y25, RegWrite);
  and and_10 (in28, y28, RegWrite);
  and and_11 (in31, y31, RegWrite);
  and and_12 (in2, y2, RegWrite);
  and and_13 (in5, y5, RegWrite);
  and and_14 (in8, y8, RegWrite);
  and and_15 (in11, y11, RegWrite);
  and and_16 (in14, y14, RegWrite);
  and and_17 (in17, y17, RegWrite);
  and and_18 (in20, y20, RegWrite);
  and and_19 (in23, y23, RegWrite);
  and and_20 (in26, y26, RegWrite);
  and and_21 (in29, y29, RegWrite);
  and and_22 (in3, y3, RegWrite);
  and and_23 (in6, y6, RegWrite);
  and and_24 (in9, y9, RegWrite);
  and and_25 (in12, y12, RegWrite);
  and and_26 (in15, y15, RegWrite);
  and and_27 (in18, y18, RegWrite);
  and and_28 (in21, y21, RegWrite);
  and and_29 (in24, y24, RegWrite);
  and and_30 (in27, y27, RegWrite);
  and and_31 (in30, y30, RegWrite);
  Register #(.Bits(32)) Reg_0 (.D(WriteData), .C(Clock), .en(1'b0), .Q(Reg0out));
  Register #(.Bits(32)) Reg_5 (.D(WriteData), .C(Clock), .en(in5), .Q(Reg5out));
  Register #(.Bits(32)) Reg_10 (.D(WriteData), .C(Clock), .en(in10), .Q(Reg10out));
  Register #(.Bits(32)) Reg_15 (.D(WriteData), .C(Clock), .en(in15), .Q(Reg15out));
  Register #(.Bits(32)) Reg_20 (.D(WriteData), .C(Clock), .en(in20), .Q(Reg20out));
  Register #(.Bits(32)) Reg_25 (.D(WriteData), .C(Clock), .en(in25), .Q(Reg25out));
  Register #(.Bits(32)) Reg_30 (.D(WriteData), .C(Clock), .en(in30), .Q(Reg30out));
  Register #(.Bits(32)) Reg_1 (.D(WriteData), .C(Clock), .en(in1), .Q(Reg1out));
  Register #(.Bits(32)) Reg_6 (.D(WriteData), .C(Clock), .en(in6), .Q(Reg6out));
  Register #(.Bits(32)) Reg_11 (.D(WriteData), .C(Clock), .en(in11), .Q(Reg11out));
  Register #(.Bits(32)) Reg_16 (.D(WriteData), .C(Clock), .en(in16), .Q(Reg16out));
  Register #(.Bits(32)) Reg_21 (.D(WriteData), .C(Clock), .en(in21), .Q(Reg21out));
  Register #(.Bits(32)) Reg_26 (.D(WriteData), .C(Clock), .en(in26), .Q(Reg26out));
  Register #(.Bits(32)) Reg_31 (.D(WriteData), .C(Clock), .en(in31), .Q(Reg31out));
  Register #(.Bits(32)) Reg_2 (.D(WriteData), .C(Clock), .en(in2), .Q(Reg2out));
  Register #(.Bits(32)) Reg_7 (.D(WriteData), .C(Clock), .en(in7), .Q(Reg7out));
  Register #(.Bits(32)) Reg_12 (.D(WriteData), .C(Clock), .en(in12), .Q(Reg12out));
  Register #(.Bits(32)) Reg_17 (.D(WriteData), .C(Clock), .en(in17), .Q(Reg17out));
  Register #(.Bits(32)) Reg_22 (.D(WriteData), .C(Clock), .en(in22), .Q(Reg22out));
  Register #(.Bits(32)) Reg_27 (.D(WriteData), .C(Clock), .en(in27), .Q(Reg27out));
  Multiplexer #(.Bits(32), .Selector_Bits(5)) multiplexer_1 (
    .sel(ReadReg1), .in_0(Reg0out), .in_1(Reg1out), .in_2(Reg2out), .in_3(Reg3out), .in_4(Reg4out),
    .in_5(Reg5out), .in_6(Reg6out), .in_7(Reg7out), .in_8(Reg8out), .in_9(Reg9out), .in_10(Reg10out),
    .in_11(Reg11out), .in_12(Reg12out), .in_13(Reg13out), .in_14(Reg14out), .in_15(Reg15out),
    .in_16(Reg16out), .in_17(Reg17out), .in_18(Reg18out), .in_19(Reg19out), .in_20(Reg20out),
    .in_21(Reg21out), .in_22(Reg22out), .in_23(Reg23out), .in_24(Reg24out), .in_25(Reg25out),
    .in_26(Reg26out), .in_27(Reg27out), .in_28(Reg28out), .in_29(Reg29out), .in_30(Reg30out),
    .in_31(Reg31out), .out(ReadData1));
  Register #(.Bits(32)) Reg_3 (.D(WriteData), .C(Clock), .en(in3), .Q(Reg3out));
  Register #(.Bits(32)) Reg_8 (.D(WriteData), .C(Clock), .en(in8), .Q(Reg8out));
  Register #(.Bits(32)) Reg_13 (.D(WriteData), .C(Clock), .en(in13), .Q(Reg13out));
  Register #(.Bits(32)) Reg_18 (.D(WriteData), .C(Clock), .en(in18), .Q(Reg18out));
  Register #(.Bits(32)) Reg_23 (.D(WriteData), .C(Clock), .en(in23), .Q(Reg23out));
  Register #(.Bits(32)) Reg_28 (.D(WriteData), .C(Clock), .en(in28), .Q(Reg28out));
  Multiplexer #(.Selector_Bits(5), .Bits(32)) multiplexer_2 (
    .sel(ReadReg2), .in_0(Reg0out), .in_1(Reg1out), .in_2(Reg2out), .in_3(Reg3out), .in_4(Reg4out),
    .in_5(Reg5out), .in_6(Reg6out), .in_7(Reg7out), .in_8(Reg8out), .in_9(Reg9out), .in_10(Reg10out),
    .in_11(Reg11out), .in_12(Reg12out), .in_13(Reg13out), .in_14(Reg14out), .in_15(Reg15out),
    .in_16(Reg16out), .in_17(Reg17out), .in_18(Reg18out), .in_19(Reg19out), .in_20(Reg20out),
    .in_21(Reg21out), .in_22(Reg22out), .in_23(Reg23out), .in_24(Reg24out), .in_25(Reg25out),
    .in_26(Reg26out), .in_27(Reg27out), .in_28(Reg28out), .in_29(Reg29out), .in_30(Reg30out),
    .in_31(Reg31out), .out(ReadData2));
  Register #(.Bits(32)) Reg_4 (.D(WriteData), .C(Clock), .en(in4), .Q(Reg4out));
  Register #(.Bits(32)) Reg_9 (.D(WriteData), .C(Clock), .en(in9), .Q(Reg9out));
  Register #(.Bits(32)) Reg_14 (.D(WriteData), .C(Clock), .en(in14), .Q(Reg14out));
  Register #(.Bits(32)) Reg_19 (.D(WriteData), .C(Clock), .en(in19), .Q(Reg19out));
  Register #(.Bits(32)) Reg_24 (.D(WriteData), .C(Clock), .en(in24), .Q(Reg24out));
  Register #(.Bits(32)) Reg_29 (.D(WriteData), .C(Clock), .en(in29), .Q(Reg29out));
endmodule

/* Test case Register File Test:
WriteReg WriteData RegWrite Clock ReadReg1 ReadReg2 ReadData1 ReadData2

# $1 = 25
1 25 1 C 1 0 25 0

# $2 = 30
2 30 1 C 0 2 0 30

# $(N+1) = (N+1)
loop(N, 30)
	(N+1) (N+1) 1 C (N+1) (N) (N+1) (N)
end loop

# $(N+1) = N-60
loop(N, 30)
	(N+1) (N-60) 1 C (N+1) (N+1) (N-60) (N-60)
end loop

# Try writing to $0. This should not write anything
0 25 1 C 0 0 0 0

# try writing when RegWrite = 0
# (the registers should still have their old values)
loop(N, 30)
	(N+1) (N+80) 0 C (N+1) (N+1) (N-60) (N-60)
end loop
*/
